# Fritzing sketch 24_ring (saved by Fritzing 0.9.3b)
breadboards: 1

parts:
  Part1 = Arduino Uno (Rev3)
  24_RGB_LED_RING = 24 NeoPixel Ring [part_number=1586]
  5V_2A_Power_Supply = Power plug
  resistor = Resistor [tolerance=±5% resistance=470 package="1206 [SMD]"]
  Capacitor = Electrolytic Capacitor [capacitance=10µF package="200 mil [THT, electrolytic]"]

nets:
  N1: Part1.D6_PWM, resistor.Pin_1
  GND: Part1.GND, 24_RGB_LED_RING.GND, 5V_2A_Power_Supply.GND, Capacitor.-
  N2: 24_RGB_LED_RING.OUT, resistor.Pin_0
  VDD: 24_RGB_LED_RING.VDD, 5V_2A_Power_Supply.VCC, Capacitor.+

notes:
  G
  5V
  data INPUT

custom parts:
  24 NeoPixel Ring: 24 ultra bright smart LED NeoPixels are arranged in a circle with 2.6" (66mm) outer diameter. The rings are 'chainable' - connect the output pin of one to the input pin of another. Use only one microcontroller pin to control as many as you can chain together! Each LED is addressable as the driver chip is inside the LED. Each one has ~18mA constant current drive so the color will be very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
