# Fritzing sketch BasicLED_baterries (saved by Fritzing 0.9.3b)
breadboards: 2

parts:
  1_5V_AA_Alkaline_Battery_(x2) = Battery
  VCC2 = Battery block 9V
  3V_Coin_Cell = Battery Holders [package=battcom_20mm_pth]
  LED_(~20mA) = LED - 3mm [color="Red (633nm)" package="3 mm [THT]"]
  Resistor = Resistor [tolerance=±5% resistance=10 package=THT]
  Resistor_2 = Resistor [tolerance=±5% resistance=330 package=THT]
  LED_(~20mA)_2 = LED - 3mm [color="Red (633nm)" package="3 mm [THT]"]
  LED_(~20mA)_3 = LED - 3mm [color="Red (633nm)" package="3 mm [THT]"]

nets:
  N1: 1_5V_AA_Alkaline_Battery_(x2).+, LED_(~20mA).anode
  N2: VCC2.-, Resistor_2.Pin_1
  N3: VCC2.+, LED_(~20mA)_3.anode
  N4: 3V_Coin_Cell.+, LED_(~20mA)_2.cathode
  N5: 3V_Coin_Cell.-, LED_(~20mA)_2.anode
  N6: LED_(~20mA).cathode, Resistor.Pin_0
  N7: Resistor_2.Pin_0, LED_(~20mA)_3.cathode
