# Fritzing sketch diagram_RGBW-non-addressable (saved by Fritzing 0.9.3b)
breadboards: 1

parts:
  Part1 = Arduino Uno (Rev3)
  Q2 = npn-Powertransistor [package="TO220 [THT]"]
  Q3 = npn-Powertransistor [package="TO220 [THT]"]
  Q4 = npn-Powertransistor [package="TO220 [THT]"]
  R1 = Resistor [tolerance=±5% resistance=220 package="0603 [SMD]"]
  R2 = Resistor [tolerance=±5% resistance=220 package="0603 [SMD]"]
  R3 = Resistor [tolerance=±5% resistance=220 package=THT]
  12V_Power_Supply = Power plug
  RGB_Strip_LED2 = RGB Strip LED

nets:
  N1: Part1.D3_PWM, R2.Pin_0
  N2: Part1.D5_PWM, R1.Pin_0
  N3: Part1.D6_PWM, R3.Pin_0
  GND: Part1.GND, Q2.emitter, Q3.emitter, Q4.emitter, 12V_Power_Supply.GND
  N4: Q2.base, R3.Pin_1
  N5: Q2.collector, RGB_Strip_LED2.Green_Connect#7
  N6: Q3.base, R2.Pin_1
  N7: Q3.collector, RGB_Strip_LED2.Blue_Connect#5
  N8: Q4.base, R1.Pin_1
  N9: Q4.collector, RGB_Strip_LED2.Red_Connect#6
  N10: 12V_Power_Supply.VCC, RGB_Strip_LED2.Common_Connect#4

custom parts:
  RGB Strip LED: A tri-color Strip LED with red, green and blue. Pin order: red - common cathode - blue - green
